# Fritzing sketch NextBand (saved by Fritzing 1.0.7)
breadboards: 1

parts:
  元件1 = INMP441
  M1 = MakerFocus MAX30102
  A2 = lcd color display 1.3in 240x240 7pin interface [package=THT]
  A3 = ESP32-S3-WROOM-1-N16R8 dev board

nets:
  N1: 元件1.WS, A3.Pin_16
  N2: 元件1.SCK, A3.Pin_15
  N3: 元件1.SD, A3.Pin_14
  VDD: 元件1.VDD, M1.VIN, A2.VCC, A3.Pin_1, A3.Pin_2
  GND: 元件1.GND, M1.GND, A2.GND, A3.Pin_22, A3.Pin_23, A3.Pin_24, A3.Pin_44
  N4: M1.SCL, A3.Pin_12
  N5: M1.SDA, A3.Pin_11
  N6: A2.SCL, A3.Pin_18
  N7: A2.SDA, A3.Pin_17
  N8: A2.RES, A3.Pin_4
  N9: A2.DC, A3.Pin_5
  N10: A2.CS, A3.Pin_6

notes:
  K2
  K1
  K3
  K4

custom parts:
  INMP441: This is a simple breakout board for the INMP441 I2S MEMS microphone.
  MakerFocus MAX30102: Oximeter module using the MAX30102 chip. As usual, if you want the mounting holes in pcb, you need to drag a hole over the pad in silkscreen to actually drill the hole (by default they are not drilled)
  lcd color display 1.3in 240x240 7pin interface: 1.3 Inch Color 240 x 240 IPS TFT LCD Display Screen Module Board 7 Pin 4 Wire ST7789VW Drive IC SPI interface.
  ESP32-S3-WROOM-1-N16R8 dev board: ESP32-S3 WIFI+BLE5.0 Development Board ESP32-S3-WROOM-1-N16R8(16M Flash/8SRAM).
